# Fritzing sketch 3_bit_adder_2 (saved by Fritzing 0.9.3b)
circuit board: 22.4787cm x 13.9357cm
breadboards: 4

parts:
  LCD1 = LCD screen
  Part1 = Arduino Uno (Rev3)
  R1_220Ohm = Resistor [tolerance=±5% resistance=220 package=THT]
  U1_Pot_10kOhm = POT [package=3362u]
  IC1_NOT_1st-bit = DIP - 16 pins [chip_label=4049 package="DIP (Dual Inline) [THT]"]
  IC2_OR_1st-bit = 4071 4 x 2 Input OR Gate, multi-part [part_number=4071 package="DIP (Dual Inline) [THT]"]
  IC2_OR_1st-bit_2 = 4071_4_x_2_input_OR_gate_multipart_subpart1 [part_number=4071]
  IC2_OR_1st-bit_1 = 4071_4_x_2_input_OR_gate_multipart_subpart2 [part_number=4071]
  IC2_OR_1st-bit_2 = 4071_4_x_2_input_OR_gate_multipart_subpart3 [part_number=4071]
  IC3_AND_I_1st-bit = 4081 4 x 2 Input AND Gate, multi-part [part_number=4081 package="DIP (Dual Inline) [THT]"]
  IC3_AND_I_1st-bit_2 = 4081_4_x_2_input_AND_gate_multipart_subpart1 [part_number=4081]
  IC3_AND_I_1st-bit_1 = 4081_4_x_2_input_AND_gate_multipart_subpart2 [part_number=4081]
  IC3_AND_I_1st-bit_2 = 4081_4_x_2_input_AND_gate_multipart_subpart3 [part_number=4081]
  IC3_AND_I_1st-bit_3 = 4081_4_x_2_input_AND_gate_multipart_subpart4 [part_number=4081]
  IC4_AND_II_1st-bit = 4081 4 x 2 Input AND Gate, multi-part [part_number=4081 package="DIP (Dual Inline) [THT]"]
  IC4_AND_II_1st-bit_2 = 4081_4_x_2_input_AND_gate_multipart_subpart1 [part_number=4081]
  SW1 = DIP Switch 8 Position [package=dipswitch-08]
  R7_Y_1 = Resistor [tolerance=±20% resistance=10k package=THT]
  R6_Y_2 = Resistor [tolerance=±20% resistance=10k package=THT]
  R5_X_0 = Resistor [tolerance=±20% resistance=10k package=THT]
  R4_X_1 = Resistor [tolerance=±20% resistance=10k package=THT]
  R3_X_2 = Resistor [tolerance=±20% resistance=10k package=THT]
  R2_C_IN = Resistor [tolerance=±20% resistance=10k package=THT]
  R8_Y_0 = Resistor [tolerance=±20% resistance=10k package=THT]

nets:
  VSS: LCD1.VSS, LCD1.R/W, LCD1.LED-, Part1.GND, U1_Pot_10kOhm.E, IC1_NOT_1st-bit.VSS(GND), IC2_OR_1st-bit.connector6, IC2_OR_1st-bit_2.connector6, IC3_AND_I_1st-bit.connector6, IC3_AND_I_1st-bit_2.connector6, IC4_AND_II_1st-bit.connector6, IC4_AND_II_1st-bit_2.connector6, R7_Y_1.Pin_0, R6_Y_2.Pin_0, R5_X_0.Pin_0, R4_X_1.Pin_0, R3_X_2.Pin_0, R2_C_IN.Pin_0, R8_Y_0.Pin_0
  VDD: LCD1.VDD, Part1.5V, R1_220Ohm.Pin_0, U1_Pot_10kOhm.A, IC1_NOT_1st-bit.VDD, IC2_OR_1st-bit.connector13, IC2_OR_1st-bit_2.connector13, IC3_AND_I_1st-bit.connector13, IC3_AND_I_1st-bit_2.connector13, IC4_AND_II_1st-bit.connector13, IC4_AND_II_1st-bit_2.connector13, SW1.9, SW1.10, SW1.11, SW1.12, SW1.13, SW1.14, SW1.15
  N1: LCD1.V0, U1_Pot_10kOhm.S
  N2: LCD1.RS, Part1.D12/MISO
  N3: LCD1.E, Part1.D11_PWM/MOSI
  N4: LCD1.DB4, Part1.D5_PWM
  N5: LCD1.DB5, Part1.D4
  N6: LCD1.DB6, Part1.D3_PWM
  N7: LCD1.DB7, Part1.D2
  N8: LCD1.LED+, R1_220Ohm.Pin_1
  N9: Part1.A5/SCL, IC2_OR_1st-bit.connector3
  N10: IC1_NOT_1st-bit.C, IC3_AND_I_1st-bit.connector1, IC3_AND_I_1st-bit.connector7, IC3_AND_I_1st-bit_1.connector1, IC3_AND_I_1st-bit_3.connector7, SW1.5, R5_X_0.Pin_1
  N11: IC2_OR_1st-bit.connector0, IC3_AND_I_1st-bit.connector2
  N12: IC2_OR_1st-bit.connector1, IC3_AND_I_1st-bit.connector3
  N13: IC2_OR_1st-bit.connector2, IC2_OR_1st-bit.connector4
  N14: IC2_OR_1st-bit.connector5, IC3_AND_I_1st-bit.connector9
  N15: IC2_OR_1st-bit_1.connector0, IC3_AND_I_1st-bit_1.connector2
  N16: IC2_OR_1st-bit_1.connector1, IC3_AND_I_1st-bit_2.connector3
  N17: IC2_OR_1st-bit_1.connector2, IC2_OR_1st-bit_2.connector4
  N18: IC2_OR_1st-bit_2.connector5, IC3_AND_I_1st-bit_3.connector9
  N19: IC3_AND_I_1st-bit.connector0, IC3_AND_I_1st-bit.connector4, IC3_AND_I_1st-bit_1.connector0, IC3_AND_I_1st-bit_2.connector4, SW1.2, R2_C_IN.Pin_1
  N20: IC3_AND_I_1st-bit.connector5, IC3_AND_I_1st-bit.connector8, IC3_AND_I_1st-bit_2.connector5, IC3_AND_I_1st-bit_3.connector8, SW1.8, R8_Y_0.Pin_1
  N21: SW1.3, R3_X_2.Pin_1
  N22: SW1.4, R4_X_1.Pin_1
  N23: SW1.6, R6_Y_2.Pin_1
  N24: SW1.7, R7_Y_1.Pin_1

custom parts:
  DIP - 16 pins: A DIP stand-in part for whatever IC you want. With 16 pins on a 300mil dual inline package (DIP) footprint.
