# Fritzing sketch 3_bit_adder_final (saved by Fritzing 0.9.3b)
circuit board: 34.8997cm x 10.6805cm
breadboards: 6

parts:
  LCD1 = LCD screen
  Part1 = Arduino Uno (Rev3)
  R1_220Ohm = Resistor [tolerance=±5% resistance=220 package=THT]
  U1_Pot_10kOhm = POT [package=3362u]
  IC1_NOT_1st-bit = DIP - 16 pins [chip_label=4049 package="DIP (Dual Inline) [THT]"]
  IC2_OR_1st-bit = 4071 4 x 2 Input OR Gate, multi-part [part_number=4071 package="DIP (Dual Inline) [THT]"]
  IC2_OR_1st-bit_2 = 4071_4_x_2_input_OR_gate_multipart_subpart1 [part_number=4071]
  IC2_OR_1st-bit_1 = 4071_4_x_2_input_OR_gate_multipart_subpart2 [part_number=4071]
  IC2_OR_1st-bit_2 = 4071_4_x_2_input_OR_gate_multipart_subpart3 [part_number=4071]
  IC2_OR_1st-bit_3 = 4071_4_x_2_input_OR_gate_multipart_subpart4 [part_number=4071]
  IC2_OR_1st-bit_4 = 4071_4_x_2_input_OR_gate_multipart_subpart5 [part_number=4071]
  IC3_AND_I_1st-bit = 4081 4 x 2 Input AND Gate, multi-part [part_number=4081 package="DIP (Dual Inline) [THT]"]
  IC3_AND_I_1st-bit_2 = 4081_4_x_2_input_AND_gate_multipart_subpart1 [part_number=4081]
  IC3_AND_I_1st-bit_1 = 4081_4_x_2_input_AND_gate_multipart_subpart2 [part_number=4081]
  IC3_AND_I_1st-bit_2 = 4081_4_x_2_input_AND_gate_multipart_subpart3 [part_number=4081]
  IC3_AND_I_1st-bit_3 = 4081_4_x_2_input_AND_gate_multipart_subpart4 [part_number=4081]
  IC4_AND_II_1st-bit = 4081 4 x 2 Input AND Gate, multi-part [part_number=4081 package="DIP (Dual Inline) [THT]"]
  IC4_AND_II_1st-bit_2 = 4081_4_x_2_input_AND_gate_multipart_subpart1 [part_number=4081]
  IC4_AND_II_1st-bit_1 = 4081_4_x_2_input_AND_gate_multipart_subpart2 [part_number=4081]
  IC4_AND_II_1st-bit_2 = 4081_4_x_2_input_AND_gate_multipart_subpart3 [part_number=4081]
  IC4_AND_II_1st-bit_3 = 4081_4_x_2_input_AND_gate_multipart_subpart4 [part_number=4081]
  IC4_AND_II_1st-bit_4 = 4081_4_x_2_input_AND_gate_multipart_subpart5 [part_number=4081]
  SW1 = DIP Switch 8 Position [package=dipswitch-08]
  R7_Y_1 = Resistor [tolerance=±20% resistance=10k package=THT]
  R6_Y_2 = Resistor [tolerance=±20% resistance=10k package=THT]
  R5_X_0 = Resistor [tolerance=±20% resistance=10k package=THT]
  R4_X_1 = Resistor [tolerance=±20% resistance=10k package=THT]
  R3_X_2 = Resistor [tolerance=±20% resistance=10k package=THT]
  R2_C_IN = Resistor [tolerance=±20% resistance=10k package=THT]
  R8_Y_0 = Resistor [tolerance=±20% resistance=10k package=THT]
  IC1_NOT_2nd-bit = DIP - 16 pins [chip_label=4049 package="DIP (Dual Inline) [THT]"]
  IC2_OR_2nd-bit = 4071 4 x 2 Input OR Gate, multi-part [part_number=4071 package="DIP (Dual Inline) [THT]"]
  IC2_OR_2nd-bit_2 = 4071_4_x_2_input_OR_gate_multipart_subpart1 [part_number=4071]
  IC2_OR_2nd-bit_1 = 4071_4_x_2_input_OR_gate_multipart_subpart2 [part_number=4071]
  IC2_OR_2nd-bit_2 = 4071_4_x_2_input_OR_gate_multipart_subpart3 [part_number=4071]
  IC2_OR_2nd-bit_3 = 4071_4_x_2_input_OR_gate_multipart_subpart4 [part_number=4071]
  IC2_OR_2nd-bit_4 = 4071_4_x_2_input_OR_gate_multipart_subpart5 [part_number=4071]
  IC3_AND_I_2nd-bit = 4081 4 x 2 Input AND Gate, multi-part [part_number=4081 package="DIP (Dual Inline) [THT]"]
  IC3_AND_I_2nd-bit_2 = 4081_4_x_2_input_AND_gate_multipart_subpart1 [part_number=4081]
  IC3_AND_I_2nd-bit_1 = 4081_4_x_2_input_AND_gate_multipart_subpart2 [part_number=4081]
  IC3_AND_I_2nd-bit_2 = 4081_4_x_2_input_AND_gate_multipart_subpart3 [part_number=4081]
  IC3_AND_I_2nd-bit_3 = 4081_4_x_2_input_AND_gate_multipart_subpart4 [part_number=4081]
  IC4_AND_II_2nd-bit = 4081 4 x 2 Input AND Gate, multi-part [part_number=4081 package="DIP (Dual Inline) [THT]"]
  IC4_AND_II_2nd-bit_2 = 4081_4_x_2_input_AND_gate_multipart_subpart1 [part_number=4081]
  IC4_AND_II_2nd-bit_1 = 4081_4_x_2_input_AND_gate_multipart_subpart2 [part_number=4081]
  IC4_AND_II_2nd-bit_2 = 4081_4_x_2_input_AND_gate_multipart_subpart3 [part_number=4081]
  IC4_AND_II_2nd-bit_3 = 4081_4_x_2_input_AND_gate_multipart_subpart4 [part_number=4081]
  IC4_AND_II_2nd-bit_4 = 4081_4_x_2_input_AND_gate_multipart_subpart5 [part_number=4081]
  IC1_NOT_3rd-bit = DIP - 16 pins [chip_label=4049 package="DIP (Dual Inline) [THT]"]
  IC2_OR_3rd-bit = 4071 4 x 2 Input OR Gate, multi-part [part_number=4071 package="DIP (Dual Inline) [THT]"]
  IC2_OR_3rd-bit_2 = 4071_4_x_2_input_OR_gate_multipart_subpart1 [part_number=4071]
  IC2_OR_3rd-bit_1 = 4071_4_x_2_input_OR_gate_multipart_subpart2 [part_number=4071]
  IC2_OR_3rd-bit_2 = 4071_4_x_2_input_OR_gate_multipart_subpart3 [part_number=4071]
  IC2_OR_3rd-bit_3 = 4071_4_x_2_input_OR_gate_multipart_subpart4 [part_number=4071]
  IC2_OR_3rd-bit_4 = 4071_4_x_2_input_OR_gate_multipart_subpart5 [part_number=4071]
  IC3_AND_I_3rd-bit = 4081 4 x 2 Input AND Gate, multi-part [part_number=4081 package="DIP (Dual Inline) [THT]"]
  IC3_AND_I_3rd-bit_2 = 4081_4_x_2_input_AND_gate_multipart_subpart1 [part_number=4081]
  IC3_AND_I_3rd-bit_1 = 4081_4_x_2_input_AND_gate_multipart_subpart2 [part_number=4081]
  IC3_AND_I_3rd-bit_2 = 4081_4_x_2_input_AND_gate_multipart_subpart3 [part_number=4081]
  IC3_AND_I_3rd-bit_3 = 4081_4_x_2_input_AND_gate_multipart_subpart4 [part_number=4081]
  IC4_AND_II_3rd-bit = 4081 4 x 2 Input AND Gate, multi-part [part_number=4081 package="DIP (Dual Inline) [THT]"]
  IC4_AND_II_3rd-bit_2 = 4081_4_x_2_input_AND_gate_multipart_subpart1 [part_number=4081]
  IC4_AND_II_3rd-bit_1 = 4081_4_x_2_input_AND_gate_multipart_subpart2 [part_number=4081]
  IC4_AND_II_3rd-bit_2 = 4081_4_x_2_input_AND_gate_multipart_subpart3 [part_number=4081]
  IC4_AND_II_3rd-bit_3 = 4081_4_x_2_input_AND_gate_multipart_subpart4 [part_number=4081]
  IC4_AND_II_3rd-bit_4 = 4081_4_x_2_input_AND_gate_multipart_subpart5 [part_number=4081]

nets:
  VSS: LCD1.VSS, LCD1.R/W, LCD1.LED-, Part1.GND, U1_Pot_10kOhm.E, IC1_NOT_1st-bit.VSS(GND), IC2_OR_1st-bit.connector6, IC2_OR_1st-bit_2.connector6, IC3_AND_I_1st-bit.connector6, IC3_AND_I_1st-bit_2.connector6, IC4_AND_II_1st-bit.connector6, IC4_AND_II_1st-bit_2.connector6, R7_Y_1.Pin_0, R6_Y_2.Pin_0, R5_X_0.Pin_0, R4_X_1.Pin_0, R3_X_2.Pin_0, R2_C_IN.Pin_0, R8_Y_0.Pin_0, IC1_NOT_2nd-bit.VSS(GND), IC2_OR_2nd-bit.connector6, IC2_OR_2nd-bit_2.connector6, IC3_AND_I_2nd-bit.connector6, IC3_AND_I_2nd-bit_2.connector6, IC4_AND_II_2nd-bit.connector6, IC4_AND_II_2nd-bit_2.connector6, IC1_NOT_3rd-bit.VSS(GND), IC2_OR_3rd-bit.connector6, IC2_OR_3rd-bit_2.connector6, IC3_AND_I_3rd-bit.connector6, IC3_AND_I_3rd-bit_2.connector6, IC4_AND_II_3rd-bit.connector6, IC4_AND_II_3rd-bit_2.connector6
  VDD: LCD1.VDD, Part1.5V, R1_220Ohm.Pin_0, U1_Pot_10kOhm.A, IC1_NOT_1st-bit.VDD, IC2_OR_1st-bit.connector13, IC2_OR_1st-bit_2.connector13, IC3_AND_I_1st-bit.connector13, IC3_AND_I_1st-bit_2.connector13, IC4_AND_II_1st-bit.connector13, IC4_AND_II_1st-bit_2.connector13, SW1.9, SW1.10, SW1.11, SW1.12, SW1.13, SW1.14, SW1.15, IC1_NOT_2nd-bit.VDD, IC2_OR_2nd-bit.connector13, IC2_OR_2nd-bit_2.connector13, IC3_AND_I_2nd-bit.connector13, IC3_AND_I_2nd-bit_2.connector13, IC4_AND_II_2nd-bit.connector13, IC4_AND_II_2nd-bit_2.connector13, IC1_NOT_3rd-bit.VDD, IC2_OR_3rd-bit.connector13, IC2_OR_3rd-bit_2.connector13, IC3_AND_I_3rd-bit.connector13, IC3_AND_I_3rd-bit_2.connector13, IC4_AND_II_3rd-bit.connector13, IC4_AND_II_3rd-bit_2.connector13
  N1: LCD1.V0, U1_Pot_10kOhm.S
  N2: LCD1.RS, Part1.D12/MISO
  N3: LCD1.E, Part1.D11_PWM/MOSI
  N4: LCD1.DB4, Part1.D5_PWM
  N5: LCD1.DB5, Part1.D4
  N6: LCD1.DB6, Part1.D3_PWM
  N7: LCD1.DB7, Part1.D2
  N8: LCD1.LED+, R1_220Ohm.Pin_1
  Y_1: Part1.A0, SW1.7, R7_Y_1.Pin_1, IC1_NOT_2nd-bit.D, IC3_AND_I_2nd-bit.connector5, IC3_AND_I_2nd-bit.connector8, IC3_AND_I_2nd-bit_2.connector5, IC3_AND_I_2nd-bit_3.connector8, IC4_AND_II_2nd-bit.connector1, IC4_AND_II_2nd-bit_1.connector1
  Y_0: Part1.A1, IC1_NOT_1st-bit.D, IC3_AND_I_1st-bit.connector5, IC3_AND_I_1st-bit.connector8, IC3_AND_I_1st-bit_2.connector5, IC3_AND_I_1st-bit_3.connector8, IC4_AND_II_1st-bit.connector1, IC4_AND_II_1st-bit_1.connector1, SW1.8, R8_Y_0.Pin_1
  Result_3: Part1.A2, IC2_OR_3rd-bit.connector3, IC2_OR_3rd-bit_2.connector3
  Result_2: Part1.A3, IC2_OR_3rd-bit.connector10, IC2_OR_3rd-bit_4.connector10
  Result_1: Part1.A4/SDA, IC2_OR_2nd-bit.connector10, IC2_OR_2nd-bit_4.connector10
  Result_0: Part1.A5/SCL, IC2_OR_1st-bit.connector10, IC2_OR_1st-bit_4.connector10
  X_1: Part1.D8, SW1.4, R4_X_1.Pin_1, IC1_NOT_2nd-bit.C, IC3_AND_I_2nd-bit.connector1, IC3_AND_I_2nd-bit.connector7, IC3_AND_I_2nd-bit_1.connector1, IC3_AND_I_2nd-bit_3.connector7, IC4_AND_II_2nd-bit.connector4, IC4_AND_II_2nd-bit_2.connector4
  X_0: Part1.D9_PWM, IC1_NOT_1st-bit.C, IC3_AND_I_1st-bit.connector1, IC3_AND_I_1st-bit.connector7, IC3_AND_I_1st-bit_1.connector1, IC3_AND_I_1st-bit_3.connector7, IC4_AND_II_1st-bit.connector4, IC4_AND_II_1st-bit_2.connector4, SW1.5, R5_X_0.Pin_1
  Y_2: Part1.D13/SCK, SW1.6, R6_Y_2.Pin_1, IC1_NOT_3rd-bit.D, IC3_AND_I_3rd-bit.connector5, IC3_AND_I_3rd-bit.connector8, IC3_AND_I_3rd-bit_2.connector5, IC3_AND_I_3rd-bit_3.connector8, IC4_AND_II_3rd-bit.connector1, IC4_AND_II_3rd-bit_1.connector1
  C_IN: Part1.D6_PWM, IC1_NOT_1st-bit.F, IC3_AND_I_1st-bit.connector0, IC3_AND_I_1st-bit.connector4, IC3_AND_I_1st-bit_1.connector0, IC3_AND_I_1st-bit_2.connector4, IC4_AND_II_1st-bit.connector11, IC4_AND_II_1st-bit_4.connector11, SW1.2, R2_C_IN.Pin_1
  X_2: Part1.D7, SW1.3, R3_X_2.Pin_1, IC1_NOT_3rd-bit.C, IC3_AND_I_3rd-bit.connector1, IC3_AND_I_3rd-bit.connector7, IC3_AND_I_3rd-bit_1.connector1, IC3_AND_I_3rd-bit_3.connector7, IC4_AND_II_3rd-bit.connector4, IC4_AND_II_3rd-bit_2.connector4
  N9: IC1_NOT_1st-bit.I=~C, IC4_AND_II_1st-bit.connector0, IC4_AND_II_1st-bit_1.connector0
  N10: IC1_NOT_1st-bit.J=~D, IC4_AND_II_1st-bit.connector5, IC4_AND_II_1st-bit_2.connector5
  N11: IC1_NOT_1st-bit.E, IC2_OR_1st-bit.connector9, IC2_OR_1st-bit_3.connector9, IC4_AND_II_1st-bit.connector8, IC4_AND_II_1st-bit_3.connector8
  N12: IC1_NOT_1st-bit.K=~E, IC4_AND_II_1st-bit.connector12, IC4_AND_II_1st-bit_4.connector12
  N13: IC1_NOT_1st-bit.L=~F, IC4_AND_II_1st-bit.connector7, IC4_AND_II_1st-bit_3.connector7
  N14: IC2_OR_1st-bit.connector0, IC3_AND_I_1st-bit.connector2
  N15: IC2_OR_1st-bit.connector1, IC3_AND_I_1st-bit.connector3
  N16: IC2_OR_1st-bit.connector2, IC2_OR_1st-bit.connector4
  N17: IC2_OR_1st-bit.connector3, IC2_OR_1st-bit_2.connector3, IC1_NOT_2nd-bit.F, IC3_AND_I_2nd-bit.connector0, IC3_AND_I_2nd-bit.connector4, IC3_AND_I_2nd-bit_1.connector0, IC3_AND_I_2nd-bit_2.connector4, IC4_AND_II_2nd-bit.connector11, IC4_AND_II_2nd-bit_4.connector11
  N18: IC2_OR_1st-bit.connector5, IC3_AND_I_1st-bit.connector9
  N19: IC2_OR_1st-bit.connector7, IC4_AND_II_1st-bit.connector2
  N20: IC2_OR_1st-bit.connector8, IC4_AND_II_1st-bit.connector3
  N21: IC2_OR_1st-bit.connector11, IC4_AND_II_1st-bit.connector9
  N22: IC2_OR_1st-bit.connector12, IC4_AND_II_1st-bit.connector10
  N23: IC2_OR_1st-bit_1.connector0, IC3_AND_I_1st-bit_1.connector2
  N24: IC2_OR_1st-bit_1.connector1, IC3_AND_I_1st-bit_2.connector3
  N25: IC2_OR_1st-bit_1.connector2, IC2_OR_1st-bit_2.connector4
  N26: IC2_OR_1st-bit_2.connector5, IC3_AND_I_1st-bit_3.connector9
  N27: IC2_OR_1st-bit_3.connector7, IC4_AND_II_1st-bit_1.connector2
  N28: IC2_OR_1st-bit_3.connector8, IC4_AND_II_1st-bit_2.connector3
  N29: IC2_OR_1st-bit_4.connector11, IC4_AND_II_1st-bit_3.connector9
  N30: IC2_OR_1st-bit_4.connector12, IC4_AND_II_1st-bit_4.connector10
  N31: IC1_NOT_2nd-bit.I=~C, IC4_AND_II_2nd-bit.connector0, IC4_AND_II_2nd-bit_1.connector0
  N32: IC1_NOT_2nd-bit.J=~D, IC4_AND_II_2nd-bit.connector5, IC4_AND_II_2nd-bit_2.connector5
  N33: IC1_NOT_2nd-bit.E, IC2_OR_2nd-bit.connector9, IC2_OR_2nd-bit_3.connector9, IC4_AND_II_2nd-bit.connector8, IC4_AND_II_2nd-bit_3.connector8
  N34: IC1_NOT_2nd-bit.K=~E, IC4_AND_II_2nd-bit.connector12, IC4_AND_II_2nd-bit_4.connector12
  N35: IC1_NOT_2nd-bit.L=~F, IC4_AND_II_2nd-bit.connector7, IC4_AND_II_2nd-bit_3.connector7
  N36: IC2_OR_2nd-bit.connector0, IC3_AND_I_2nd-bit.connector2
  N37: IC2_OR_2nd-bit.connector1, IC3_AND_I_2nd-bit.connector3
  N38: IC2_OR_2nd-bit.connector2, IC2_OR_2nd-bit.connector4
  N39: IC2_OR_2nd-bit.connector3, IC2_OR_2nd-bit_2.connector3, IC1_NOT_3rd-bit.F, IC3_AND_I_3rd-bit.connector0, IC3_AND_I_3rd-bit.connector4, IC3_AND_I_3rd-bit_1.connector0, IC3_AND_I_3rd-bit_2.connector4, IC4_AND_II_3rd-bit.connector11, IC4_AND_II_3rd-bit_4.connector11
  N40: IC2_OR_2nd-bit.connector5, IC3_AND_I_2nd-bit.connector9
  N41: IC2_OR_2nd-bit.connector7, IC4_AND_II_2nd-bit.connector2
  N42: IC2_OR_2nd-bit.connector8, IC4_AND_II_2nd-bit.connector3
  N43: IC2_OR_2nd-bit.connector11, IC4_AND_II_2nd-bit.connector9
  N44: IC2_OR_2nd-bit.connector12, IC4_AND_II_2nd-bit.connector10
  N45: IC2_OR_2nd-bit_1.connector0, IC3_AND_I_2nd-bit_1.connector2
  N46: IC2_OR_2nd-bit_1.connector1, IC3_AND_I_2nd-bit_2.connector3
  N47: IC2_OR_2nd-bit_1.connector2, IC2_OR_2nd-bit_2.connector4
  N48: IC2_OR_2nd-bit_2.connector5, IC3_AND_I_2nd-bit_3.connector9
  N49: IC2_OR_2nd-bit_3.connector7, IC4_AND_II_2nd-bit_1.connector2
  N50: IC2_OR_2nd-bit_3.connector8, IC4_AND_II_2nd-bit_2.connector3
  N51: IC2_OR_2nd-bit_4.connector11, IC4_AND_II_2nd-bit_3.connector9
  N52: IC2_OR_2nd-bit_4.connector12, IC4_AND_II_2nd-bit_4.connector10
  N53: IC1_NOT_3rd-bit.I=~C, IC4_AND_II_3rd-bit.connector0, IC4_AND_II_3rd-bit_1.connector0
  N54: IC1_NOT_3rd-bit.J=~D, IC4_AND_II_3rd-bit.connector5, IC4_AND_II_3rd-bit_2.connector5
  N55: IC1_NOT_3rd-bit.E, IC2_OR_3rd-bit.connector9, IC2_OR_3rd-bit_3.connector9, IC4_AND_II_3rd-bit.connector8, IC4_AND_II_3rd-bit_3.connector8
  N56: IC1_NOT_3rd-bit.K=~E, IC4_AND_II_3rd-bit.connector12, IC4_AND_II_3rd-bit_4.connector12
  N57: IC1_NOT_3rd-bit.L=~F, IC4_AND_II_3rd-bit.connector7, IC4_AND_II_3rd-bit_3.connector7
  N58: IC2_OR_3rd-bit.connector0, IC3_AND_I_3rd-bit.connector2
  N59: IC2_OR_3rd-bit.connector1, IC3_AND_I_3rd-bit.connector3
  N60: IC2_OR_3rd-bit.connector2, IC2_OR_3rd-bit.connector4
  N61: IC2_OR_3rd-bit.connector5, IC3_AND_I_3rd-bit.connector9
  N62: IC2_OR_3rd-bit.connector7, IC4_AND_II_3rd-bit.connector2
  N63: IC2_OR_3rd-bit.connector8, IC4_AND_II_3rd-bit.connector3
  N64: IC2_OR_3rd-bit.connector11, IC4_AND_II_3rd-bit.connector9
  N65: IC2_OR_3rd-bit.connector12, IC4_AND_II_3rd-bit.connector10
  N66: IC2_OR_3rd-bit_1.connector0, IC3_AND_I_3rd-bit_1.connector2
  N67: IC2_OR_3rd-bit_1.connector1, IC3_AND_I_3rd-bit_2.connector3
  N68: IC2_OR_3rd-bit_1.connector2, IC2_OR_3rd-bit_2.connector4
  N69: IC2_OR_3rd-bit_2.connector5, IC3_AND_I_3rd-bit_3.connector9
  N70: IC2_OR_3rd-bit_3.connector7, IC4_AND_II_3rd-bit_1.connector2
  N71: IC2_OR_3rd-bit_3.connector8, IC4_AND_II_3rd-bit_2.connector3
  N72: IC2_OR_3rd-bit_4.connector11, IC4_AND_II_3rd-bit_3.connector9
  N73: IC2_OR_3rd-bit_4.connector12, IC4_AND_II_3rd-bit_4.connector10

custom parts:
  DIP - 16 pins: A DIP stand-in part for whatever IC you want. With 16 pins on a 300mil dual inline package (DIP) footprint.
